# Fritzing sketch switch2serial (saved by Fritzing 0.9.2b)
circuit board: 8.46667cm x 5.64444cm
breadboards: 1

parts:
  Part1 = Arduino Uno (Rev3)
  R2 = Resistor [tolerance=±5% resistance=220 package=THT]
  R3 = Resistor [tolerance=±5% resistance=220 package=THT]
  R1 = Slide Potentiometer [maximum_resistance=10kΩ]
  S2 = Round Pushbutton

nets:
  N1: Part1.A0, R1.wiper
  N2: Part1.D2, R3.Pin_0, S2.leg0
  N3: Part1.GND, R2.Pin_0, R3.Pin_1
  N4: Part1.VIN, R1.leg2, S2.leg1
  N5: R2.Pin_1, R1.leg1
